# Fritzing sketch Untitled Sketch (saved by Fritzing 0.9.3b)

parts:
  Part1 = Arduino Uno (Rev3)
  R1 = Rotary Potentiometer (Small) [maximum_resistance=100kΩ package=THT]
  920KV_Motor3 = DJI 920 KV Motor  # not connected
  M2 = ESC
  BAT1 = Battery Holders [package=battery-aaa]  # not connected

nets:
  N1: Part1.A0, R1.wiper
  N2: Part1.D8, M2.DATA
  3V3: Part1.3V3, M2.5V
  N3: Part1.5V, R1.leg1
  GND: Part1.GND, R1.leg2, M2.GND

custom parts:
  DJI 920 KV Motor: DJI Brushless Outrunner 2212/920K Motor F330-550
